# Fritzing sketch Wiring Diagram (saved by Fritzing 0.9.3b)
breadboards: 1

parts:
  Part2 = Adafruit 2.13in eInk Under FeatherWing [part_number="Adafruit #4128"]  # not connected
  Part3 = Adafruit HUZZAH32 ESP32 Feather [part_number="Adafruit #3405"]  # not connected
  PART1 = SparkFun Soil Moisture Sensor [part_number=SEN-13322]
  KEYPAD1 = Membrane Matrix Keypad  # not connected
  hc-sr1 = hc-sr04  # not connected
  Part4 = Adafruit DC+Stepper FeatherWing [part_number="Adafruit #2927"]
  Part5 = Adafruit Adalogger FeatherWing [part_number="Adafruit #2922"]  # not connected
  J1 = Piezo Speaker  # not connected
  J2 = Basic Servo  # not connected
  M1 = DC Motor
  VCC1 = 4 x AAA Battery Mount  # not connected

nets:
  VCC: PART1.VCC, Part4.+3.3V
  GND: PART1.GND, Part4.GND
  N1: PART1.SIG, Part4.MOSI
  N2: Part4.M2A, M1.pin_1
  N3: Part4.M2B, M1.pin_2

notes:
  These connect to eachother directly
  This is connected through an
  These 3 components are not currently connected but will be used in further expansion
  The esp32 feather is the bottom board on the stack
  The rest stack on top in order shown
  (going from top to bottom)

custom parts:
  Adafruit 2.13in eInk Under FeatherWing: Easy e-paper finally comes to your Feather, with this breakout that's designed to make it a breeze to add a tri-color eInk display. Chances are you've seen one of those new-fangled 'e-readers' like the Kindle or Nook. They have gigantic electronic paper 'static' displays - that means the image stays on the display even when power is completely disconnected. The image is also high contrast and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
  SparkFun Soil Moisture Sensor: The SparkFun Soil Moisture Sensor is a simple breakout for measuring the moisture in soil and similar materials.
  Membrane Matrix Keypad: Membrane Matrix 3x4 Keypad
  Adafruit DC+Stepper FeatherWing: This is the DC Motor + Stepper FeatherWing which will let you use 2 x bi-polar stepper motors or 4 x brushed DC motorx (or 1 stepper and 2 DC motors). Using our Feather Stacking Headers or Feather Female Headers you can connect a FeatherWing on top or bottom of your Feather board and let the board take flight! The original Adafruit Motorshield Kit is one of our most beloved kits, which is why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
  Adafruit Adalogger FeatherWing: This is the Adalogger FeatherWing: it adds both a battery-backed Real Time Clock and micro SD card storage to any Feather main board. This FeatherWing will make it real easy to add datalogging to any of our existing Feathers. You get both an I2C real time clock (PCF8523) with 32KHz crystal and battery backup, and a microSD socket that connects to the SPI port pins (+ extra pin for CS). Tested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
